// Logisim project 8BITALU.circ as structural Verilog: 3 circuits, main circuit ALU
module ALU (
  input  F2,
  input  F1,
  input  F0,
  input  Cin,
  input  M,
  input  B7,
  input  in_7,
  input  in_8,
  input  in_9,
  input  in_10,
  input  in_11,
  input  in_12,
  input  B0,
  input  A7,
  input  in_15,
  input  in_16,
  input  in_17,
  input  in_18,
  input  in_19,
  input  in_20,
  input  A0
);

  wire n1bit_1_cout, n1bit_2_cout, n1bit_3_cout, n1bit_5_cout, n1bit_6_cout, n1bit_7_cout, n1bit_8_cout,
       or_1_out;

  or or_1 (or_1_out, Cin, M);
  _1BIT u_1bit_1 (.F2(F2), .F1(F1), .F0(F0), .Cin(n1bit_8_cout), .Cout(n1bit_1_cout));  // open: B, A, A_B, S
  _1BIT u_1bit_2 (.F2(F2), .F1(F1), .F0(F0), .Cin(n1bit_1_cout), .Cout(n1bit_2_cout));  // open: B, A, A_B, S
  _1BIT u_1bit_3 (.F2(F2), .F1(F1), .F0(F0), .Cin(n1bit_2_cout), .Cout(n1bit_3_cout));  // open: B, A, A_B, S
  _1BIT u_1bit_4 (.F2(F2), .F1(F1), .F0(F0), .Cin(n1bit_3_cout));  // open: B, A, A_B, Cout, S
  B_XOR_M b_xor_m_1 (
    .M(M), .B7(B7), .B6(in_7), .B5(in_8), .B4(in_9), .B3(in_10), .B2(in_11), .B1(in_12), .B0(B0));  // open: M_2, B7_prime, B6_prime, B5_prime, B4_prime, B3_prime, B2_prime, B1_prime, B0_prime
  _1BIT u_1bit_5 (.F2(F2), .F1(F1), .F0(F0), .Cin(or_1_out), .Cout(n1bit_5_cout));  // open: B, A, A_B, S
  _1BIT u_1bit_6 (.F2(F2), .F1(F1), .F0(F0), .Cin(n1bit_5_cout), .Cout(n1bit_6_cout));  // open: B, A, A_B, S
  _1BIT u_1bit_7 (.F2(F2), .F1(F1), .F0(F0), .Cin(n1bit_6_cout), .Cout(n1bit_7_cout));  // open: B, A, A_B, S
  _1BIT u_1bit_8 (.F2(F2), .F1(F1), .F0(F0), .Cin(n1bit_7_cout), .Cout(n1bit_8_cout));  // open: B, A, A_B, S
endmodule

module B_XOR_M (
  input  B7,
  input  B6,
  input  B5,
  input  B4,
  input  B3,
  input  B2,
  input  B1,
  input  B0,
  input  M,
  output M_2,
  output B7_prime,
  output B6_prime,
  output B5_prime,
  output B4_prime,
  output B3_prime,
  output B2_prime,
  output B1_prime,
  output B0_prime
);

  xor xor_1 (B7_prime, B7, M);
  xor xor_2 (B6_prime, B6, M);
  xor xor_3 (B4_prime, B4, M);
  xor xor_4 (B5_prime, B5, M);
  xor xor_5 (B3_prime, B3, M);
  xor xor_6 (B2_prime, B2, M);
  xor xor_7 (B1_prime, B1, M);
  xor xor_8 (B0_prime, B0, M);

  assign M_2 = M;
endmodule

module _1BIT (
  input  F2,
  input  F1,
  input  F0,
  input  Cin,
  input  B,
  input  A,
  output A_B,
  output Cout,
  output S
);

  wire and_1_out, and_2_out, and_3_out, and_4_out, and_5_out, and_6_out, and_7_out, and_8_out, and_9_out,
       and_10_out, and_11_out, and_12_out, and_13_out, and_14_out, and_15_out, not_1_out, not_2_out,
       not_3_out, not_4_out, not_5_out, not_6_out;

  not not_1 (not_1_out, F2);
  not not_2 (not_2_out, F1);
  not not_3 (not_3_out, F0);
  not not_4 (not_4_out, Cin);
  not not_5 (not_5_out, B);
  not not_6 (not_6_out, A);
  and and_1 (and_1_out, not_1_out, not_2_out, not_3_out, A, B);
  and and_2 (and_2_out, not_1_out, not_2_out, not_3_out, A, Cin);
  and and_3 (and_3_out, not_1_out, not_2_out, not_3_out, B, Cin);
  and and_4 (and_4_out, not_2_out, not_3_out, not_4_out, not_5_out, A);
  and and_5 (and_5_out, not_2_out, not_3_out, not_4_out, not_6_out, B);
  and and_6 (and_6_out, not_1_out, not_3_out, not_5_out, not_6_out, Cin);
  and and_7 (and_7_out, not_2_out, not_3_out, A, B, Cin);
  and and_8 (and_8_out, not_1_out, not_2_out, A, B, F0);
  and and_9 (and_9_out, not_1_out, not_6_out, F1);
  and and_10 (and_10_out, not_5_out, not_6_out, F1);
  and and_11 (and_11_out, not_1_out, not_5_out, F0, F1);
  and and_12 (and_12_out, not_2_out, not_5_out, A, F2);
  and and_13 (and_13_out, not_2_out, not_3_out, B, F2);
  and and_14 (and_14_out, not_2_out, not_6_out, B, F2);
  and and_15 (and_15_out, A, B, F0, F1, F2);
  xor xor_1 (A_B, B, A);
  or or_1 (Cout, and_1_out, and_2_out, and_3_out);
  or or_2 (S, and_4_out, and_5_out, and_6_out, and_7_out, and_8_out, and_9_out, and_10_out, and_11_out, and_12_out, and_13_out, and_14_out, and_15_out);
endmodule
