// Logisim project 8_Bit_ALU.circ as structural Verilog: 1 circuit, main circuit CMP
module CMP (
  input  A7,
  input  A6,
  input  A5,
  input  A4,
  input  A3,
  input  A2,
  input  A1,
  input  A0,
  input  B7,
  input  B6,
  input  B5,
  input  B4,
  input  B3,
  input  B2,
  input  B1,
  input  B0,
  output A_B,
  output A_B_2
);

  wire and_1_out, and_2_out, and_3_out, and_4_out, and_5_out, and_6_out, and_7_out, and_8_out, and_9_out,
       and_10_out, and_11_out, and_12_out, and_13_out, and_14_out, and_15_out, and_16_out, and_17_out,
       and_18_out, and_19_out, and_20_out, and_21_out, and_22_out, and_23_out, and_24_out, and_25_out,
       and_26_out, and_27_out, and_28_out, and_29_out, nand_1_out, nand_2_out, nand_3_out, nand_4_out,
       nand_5_out, nand_6_out, nand_7_out, nand_8_out, not_1_out, not_2_out, not_3_out, not_4_out, not_5_out,
       not_6_out, not_7_out, not_8_out, or_1_out, or_2_out, or_3_out, or_4_out, or_5_out, or_6_out, or_7_out,
       or_8_out, or_9_out, or_10_out, or_11_out, or_12_out, or_13_out, or_14_out;

  and and_1 (and_1_out, A7, and_2_out);
  and and_2 (and_2_out, nand_1_out, or_1_out);
  not not_1 (not_1_out, and_2_out);
  or or_1 (or_1_out, A7, B7);
  nand nand_1 (nand_1_out, A7, B7);
  and and_3 (and_3_out, nand_2_out, or_3_out);
  and and_4 (and_4_out, A6, not_1_out);
  not not_2 (not_2_out, and_3_out);
  or or_2 (or_2_out, and_1_out, and_5_out);
  and and_5 (and_5_out, and_4_out, and_3_out);
  and and_6 (and_6_out, not_2_out, not_1_out);
  nand nand_2 (nand_2_out, A6, B6);
  or or_3 (or_3_out, A6, B6);
  and and_7 (and_7_out, A5, and_6_out);
  not not_3 (not_3_out, and_9_out);
  and and_8 (and_8_out, and_7_out, and_9_out);
  and and_9 (and_9_out, nand_3_out, or_4_out);
  and and_10 (and_10_out, not_3_out, and_6_out);
  nand nand_3 (nand_3_out, A5, B5);
  or or_4 (or_4_out, A5, B5);
  or or_5 (or_5_out, or_2_out, and_8_out);
  and and_11 (and_11_out, A4, and_10_out);
  and and_12 (and_12_out, and_11_out, and_13_out);
  and and_13 (and_13_out, nand_4_out, or_6_out);
  not not_4 (not_4_out, and_13_out);
  and and_14 (and_14_out, not_4_out, and_10_out);
  or or_6 (or_6_out, A4, B4);
  or or_7 (or_7_out, or_5_out, and_12_out);
  and and_15 (and_15_out, A3, and_14_out);
  nand nand_4 (nand_4_out, A4, B4);
  and and_16 (and_16_out, and_15_out, and_17_out);
  and and_17 (and_17_out, nand_5_out, or_8_out);
  not not_5 (not_5_out, and_17_out);
  and and_18 (and_18_out, not_5_out, and_14_out);
  or or_8 (or_8_out, A3, B3);
  or or_9 (or_9_out, or_7_out, and_16_out);
  nand nand_5 (nand_5_out, A3, B3);
  and and_19 (and_19_out, nand_6_out, or_11_out);
  and and_20 (and_20_out, A2, and_18_out);
  not not_6 (not_6_out, and_19_out);
  or or_10 (or_10_out, or_9_out, and_21_out);
  and and_21 (and_21_out, and_20_out, and_19_out);
  and and_22 (and_22_out, not_6_out, and_18_out);
  nand nand_6 (nand_6_out, A2, B2);
  or or_11 (or_11_out, A2, B2);
  and and_23 (and_23_out, A1, and_22_out);
  not not_7 (not_7_out, and_25_out);
  and and_24 (and_24_out, and_23_out, and_25_out);
  and and_25 (and_25_out, nand_7_out, or_12_out);
  and and_26 (and_26_out, not_7_out, and_22_out);
  nand nand_7 (nand_7_out, A1, B1);
  or or_12 (or_12_out, A1, B1);
  or or_13 (or_13_out, or_10_out, and_24_out);
  and and_27 (and_27_out, A0, and_26_out);
  and and_28 (and_28_out, and_27_out, and_29_out);
  and and_29 (and_29_out, nand_8_out, or_14_out);
  not not_8 (not_8_out, and_29_out);
  and and_30 (A_B_2, not_8_out, and_26_out);
  or or_14 (or_14_out, A0, B0);
  or or_15 (A_B, or_13_out, and_28_out);
  nand nand_8 (nand_8_out, A0, B0);
endmodule
